# Fritzing sketch clock (saved by Fritzing 0.9.4)
breadboards: 1

parts:
  Part1 = Arduino Leonardo (Rev3b)
  7_Segment1 = 7 Segment Display
  Common_Anode = 7 Segment Display
  7_Segment2 = 7 Segment Display
  7_Segment3 = 7 Segment Display
  R1 = Resistor [tolerance=±5% resistance=220 package=THT]
  R3 = Resistor [tolerance=±5% resistance=220 package=THT]
  R4 = Resistor [tolerance=±5% resistance=220 package=THT]
  R5 = Resistor [tolerance=±5% resistance=220 package=THT]
  R6 = Resistor [tolerance=±5% resistance=220 package=THT]
  R7 = Resistor [tolerance=±5% resistance=220 package=THT]
  R8 = Resistor [tolerance=±5% resistance=220 package=THT]
  R9 = Resistor [tolerance=±5% resistance=220 package=THT]

nets:
  N1: Part1.D0/RX, 7_Segment2.common_cathode
  N2: Part1.D1/TX, R3.Pin_0
  N3: Part1.D2/SDA, R4.Pin_0
  N4: Part1.D3_PWM/SCL, Common_Anode.common_cathode
  N5: Part1.D4/A6, R1.Pin_1
  N6: Part1.D5_PWM, 7_Segment1.common_cathode
  N7: Part1.D6_PWM/A7, R5.Pin_1
  N8: Part1.D7, R6.Pin_1
  N9: Part1.5V, R9.Pin_1
  N10: Part1.D8/A8, 7_Segment3.common_cathode
  N11: Part1.D9_PWM/A9, R8.Pin_0
  N12: Part1.D10_PWM/A10, R7.Pin_0
  N13: 7_Segment1.Segment_E, Common_Anode.Segment_E, 7_Segment2.Segment_E, 7_Segment3.Segment_E, R3.Pin_1
  N14: 7_Segment1.Segment_D, Common_Anode.Segment_D, 7_Segment2.Segment_D, 7_Segment3.Segment_D, R4.Pin_1
  N15: 7_Segment1.Segment_C, Common_Anode.Segment_C, 7_Segment2.Segment_C, 7_Segment3.Segment_C, R1.Pin_0
  N16: 7_Segment1.Segment_B, Common_Anode.Segment_B, 7_Segment2.Segment_B, 7_Segment3.Segment_B, R5.Pin_0
  N17: 7_Segment1.Segment_A, Common_Anode.Segment_A, 7_Segment2.Segment_A, 7_Segment3.Segment_A, R6.Pin_0
  N18: 7_Segment1.Segment_F, Common_Anode.Segment_F, 7_Segment2.Segment_F, 7_Segment3.Segment_F, R8.Pin_1
  N19: 7_Segment1.Segment_G, Common_Anode.Segment_G, 7_Segment2.Segment_G, 7_Segment3.Segment_G, R7.Pin_1
  N20: Common_Anode.Segment_DP, R9.Pin_0
